# Fritzing sketch DHT11 Project (saved by Fritzing 0.9.9b)
breadboards: 1

parts:
  Mod1 = Raspberry Pi 4B
  Part1 = KY-015 Temperature & Humidity Sensor Module [package="Breakout board"]
  F1 = Fan - Ventilador [package=THT]

nets:
  5V: Mod1.5V, Part1.Vin, F1.5V
  GND: Mod1.GND, Part1.-, F1.GND
  N1: Mod1.GPIO4, Part1.S

custom parts:
  KY-015 Temperature & Humidity Sensor Module: DH-11 temperature and humidity sensor in KEYES KY-015 module, provides a low-latency serial interface to measure humidity and temperature.
  Fan - Ventilador: Ventilador de 2 pines, se encuentra comunmente en computadoras de escritorio
